// Logisim project problem3.circ as structural Verilog: 2 circuits, main circuit main
module main (
  input  in_1,
  input  [3:0] in_2,
  output out_3,
  output out_4,
  output out_5,
  output out_6,
  output out_7,
  output out_8,
  output out_9,
  output out_10
);

  wire clock_1_out, decoder_1_out0, decoder_1_out1, decoder_1_out2, decoder_1_out3, decoder_1_out4,
       decoder_1_out5, decoder_1_out6, decoder_1_out7;

  Clock clock_1 (.out(clock_1_out));
  Decoder #(.select(3)) decoder_1 (
    .out0(decoder_1_out0), .out1(decoder_1_out1), .out2(decoder_1_out2), .out3(decoder_1_out3),
    .out4(decoder_1_out4), .out5(decoder_1_out5), .out6(decoder_1_out6), .out7(decoder_1_out7),
    .sel(in_2[2:0]), .en(in_1));
  \logic  logic_1 (.Bs(decoder_1_out0), .b3(in_2[3]), .Clk(clock_1_out), .a(out_3));
  \logic  logic_2 (.Bs(decoder_1_out1), .b3(in_2[3]), .Clk(clock_1_out), .a(out_4));
  \logic  logic_3 (.Bs(decoder_1_out2), .b3(in_2[3]), .Clk(clock_1_out), .a(out_5));
  \logic  logic_4 (.Bs(decoder_1_out3), .b3(in_2[3]), .Clk(clock_1_out), .a(out_6));
  \logic  logic_5 (.Bs(decoder_1_out4), .b3(in_2[3]), .Clk(clock_1_out), .a(out_7));
  \logic  logic_6 (.Bs(decoder_1_out5), .b3(in_2[3]), .Clk(clock_1_out), .a(out_8));
  \logic  logic_7 (.Bs(decoder_1_out6), .b3(in_2[3]), .Clk(clock_1_out), .a(out_9));
  \logic  logic_8 (.Bs(decoder_1_out7), .b3(in_2[3]), .Clk(clock_1_out), .a(out_10));
endmodule

module \logic  (
  input  Bs,
  input  b3,
  input  Clk,
  output a
);

  wire and_1_out, and_2_out, or_1_out, xor_1_out, xor_2_out;

  xor xor_1 (xor_1_out, b3, Bs);
  xor xor_2 (xor_2_out, Bs, a);
  and and_1 (and_1_out, xor_2_out, b3);
  and and_2 (and_2_out, ~xor_1_out, a);  // AND_Gate
  D_Flip_Flop d_ff_1 (.D(or_1_out), .clk(Clk), .Q(a));  // open: Qn, preset, reset
  or or_1 (or_1_out, and_2_out, and_1_out);
endmodule
