// Logisim project cpu.circ as structural Verilog
module fetch (
  input  [63:0] PC,
  input  clk,
  output [3:0] icode,
  output [3:0] ifun,
  output [3:0] rA,
  output [3:0] rB,
  output [63:0] valC
);

  // instruction_memory instruction_memory_1: pin names not known; wires that end beside it: PC, clk, {ifun, icode}, {rB, rA}
endmodule

module instruction_memory (
  input  [63:0] PC,
  input  clk,
  output need_regids,
  output need_valC,
  output [7:0] byte_0,
  output [7:0] byte_1,
  output [7:0] byte_2,
  output [7:0] byte_3,
  output [7:0] byte_4,
  output [7:0] byte_5,
  output [7:0] byte_6,
  output [7:0] byte_7,
  output [7:0] byte_8,
  output [7:0] byte_9
);

  wire and_13_out, and_14_out, and_15_out, and_16_out, and_17_out, and_18_out, and_19_out, and_20_out,
       and_21_out, d_ff_1_q, d_ff_1_qn, decoder_1_out0, decoder_1_out1, decoder_1_out2, decoder_1_out3,
       decoder_1_out4, decoder_1_out5, decoder_1_out6, decoder_1_out7, decoder_1_out8, decoder_1_out9,
       or_1_out;
  wire [3:0] adder_1_out, and_1_out, and_2_out, and_3_out, and_4_out, and_5_out, and_6_out, and_7_out,
       and_8_out, and_9_out, and_10_out, and_11_out, and_12_out, or_2_out, or_3_out, register_1_q;
  wire [7:0] ram_1_dout;
  wire [11:0] multiplexer_1_out;

  D_Flip_Flop d_ff_1 (.D(or_1_out), .clk(clk), .Q(d_ff_1_q), .Qn(d_ff_1_qn));  // open: preset, reset
  or or_1 (or_1_out, d_ff_1_q, d_ff_1_qn);
  Subtractor subtractor_1 ();  // open: a, b, out, bin, bout
  Register #(.width(4)) register_1 (.D(adder_1_out), .en(d_ff_1_q), .clk(clk), .Q(register_1_q));  // open: clr
  Multiplexer #(.width(12)) multiplexer_1 (.out(multiplexer_1_out));  // open: in0, in1, sel
  Adder #(.width(4)) adder_1 (.a(register_1_q), .b(4'b0001), .out(adder_1_out));  // open: cin, cout
  RAM #(.addrWidth(12), .enables("line")) ram_1 (
    .addr(multiplexer_1_out), .clk(clk), .dout(ram_1_dout));  // open: we, din
  assign and_1_out = byte_0[7:4] & 4'b0010;  // AND_Gate and_1, 4 bits wide
  assign and_2_out = byte_0[7:4] & 4'b0011;  // AND_Gate and_2, 4 bits wide
  assign and_3_out = byte_0[7:4] & 4'b0100;  // AND_Gate and_3, 4 bits wide
  assign and_4_out = byte_0[7:4] & 4'b0101;  // AND_Gate and_4, 4 bits wide
  assign and_5_out = byte_0[7:4] & 4'b0110;  // AND_Gate and_5, 4 bits wide
  assign and_6_out = byte_0[7:4] & 4'b1010;  // AND_Gate and_6, 4 bits wide
  assign and_7_out = byte_0[7:4] & 4'b1011;  // AND_Gate and_7, 4 bits wide
  assign and_8_out = byte_0[7:4] & 4'b0011;  // AND_Gate and_8, 4 bits wide
  assign and_9_out = byte_0[7:4] & 4'b0100;  // AND_Gate and_9, 4 bits wide
  assign and_10_out = byte_0[7:4] & 4'b0101;  // AND_Gate and_10, 4 bits wide
  assign and_11_out = byte_0[7:4] & 4'b0111;  // AND_Gate and_11, 4 bits wide
  assign and_12_out = byte_0[7:4] & 4'b1000;  // AND_Gate and_12, 4 bits wide
  assign or_2_out = and_8_out | and_9_out | and_10_out | and_11_out | and_12_out;  // OR_Gate or_2, 4 bits wide
  assign or_3_out = and_1_out | and_2_out | and_3_out | and_4_out | and_5_out | and_6_out | and_7_out;  // OR_Gate or_3, 4 bits wide
  or or_4 (need_valC, or_2_out[0], or_2_out[1], or_2_out[2], or_2_out[3]);
  or or_5 (need_regids, or_3_out[0], or_3_out[1], or_3_out[2], or_3_out[3]);
  Decoder #(.select(4)) decoder_1 (
    .out0(decoder_1_out0), .out1(decoder_1_out1), .out2(decoder_1_out2), .out3(decoder_1_out3),
    .out4(decoder_1_out4), .out5(decoder_1_out5), .out6(decoder_1_out6), .out7(decoder_1_out7),
    .out8(decoder_1_out8), .out9(decoder_1_out9), .sel(register_1_q));  // open: out10, out11, out12, out13, out14, out15, en
  Register register_2 (.D(ram_1_dout), .en(decoder_1_out0), .clk(clk), .Q(byte_0));  // open: clr
  Register register_3 (.D(ram_1_dout), .en(and_13_out), .clk(clk), .Q(byte_1));  // open: clr
  and and_13 (and_13_out, need_regids, decoder_1_out1);
  Register register_4 (.D(ram_1_dout), .en(and_14_out), .clk(clk), .Q(byte_2));  // open: clr
  and and_14 (and_14_out, need_valC, decoder_1_out2);
  Register register_5 (.D(ram_1_dout), .en(and_15_out), .clk(clk), .Q(byte_3));  // open: clr
  and and_15 (and_15_out, need_valC, decoder_1_out3);
  Register register_6 (.D(ram_1_dout), .en(and_16_out), .clk(clk), .Q(byte_4));  // open: clr
  and and_16 (and_16_out, need_valC, decoder_1_out4);
  Register register_7 (.D(ram_1_dout), .en(and_17_out), .clk(clk), .Q(byte_5));  // open: clr
  and and_17 (and_17_out, need_valC, decoder_1_out5);
  Register register_8 (.D(ram_1_dout), .en(and_18_out), .clk(clk), .Q(byte_6));  // open: clr
  and and_18 (and_18_out, need_valC, decoder_1_out6);
  Register register_9 (.D(ram_1_dout), .en(and_19_out), .clk(clk), .Q(byte_7));  // open: clr
  and and_19 (and_19_out, need_valC, decoder_1_out7);
  Register register_10 (.D(ram_1_dout), .en(and_20_out), .clk(clk), .Q(byte_8));  // open: clr
  and and_20 (and_20_out, need_valC, decoder_1_out8);
  Register register_11 (.D(ram_1_dout), .en(and_21_out), .clk(clk), .Q(byte_9));  // open: clr
  and and_21 (and_21_out, need_valC, decoder_1_out9);
endmodule
